# Fritzing sketch motors (saved by Fritzing 0.8.7b)
breadboards: 1

parts:
  Part5 = Arduino Nano (Rev3.0)
  S3 = H-Bridge with L298N
  M5 = DC Motor
  M6 = DC Motor
  VCC1 = Battery block 9V

nets:
  GND: Part5.GND, S3.GND, VCC1.-
  N1: Part5.D3, S3.ENB
  N2: Part5.D4, S3.IN4
  N3: Part5.D5, S3.IN3
  N4: Part5.D7, S3.IN2
  N5: Part5.D8, S3.IN1
  N6: Part5.D9, S3.ENA
  VIN: Part5.VIN, S3.12V, VCC1.+
  N7: S3.M1-01, M5.pin_2
  N8: S3.M1-02, M5.pin_1
  N9: S3.M2-01, M6.pin_2
  N10: S3.M2-02, M6.pin_1

custom parts:
  H-Bridge with L298N: h-bridge
