# Fritzing sketch motors_l298 (saved by Fritzing 0.8.7b)
breadboards: 1

parts:
  Part6 = Arduino Nano (Rev3.0)
  S4 = H-Bridge with L298N
  M7 = DC Motor
  M8 = DC Motor
  VCC2 = Battery block 9V

nets:
  GND: Part6.GND, S4.GND, VCC2.-
  N1: Part6.D3, S4.ENB
  N2: Part6.D4, S4.IN4
  N3: Part6.D5, S4.IN3
  N4: Part6.D7, S4.IN2
  N5: Part6.D8, S4.IN1
  N6: Part6.D9, S4.ENA
  VIN: Part6.VIN, S4.12V, VCC2.+
  N7: S4.M1-01, M7.pin_2
  N8: S4.M1-02, M7.pin_1
  N9: S4.M2-01, M8.pin_2
  N10: S4.M2-02, M8.pin_1

custom parts:
  H-Bridge with L298N: h-bridge
