# Fritzing sketch mpu6050_monitor (saved by Fritzing 0.8.7b)
breadboards: 1

parts:
  Part2 = Arduino Nano (Rev3.0)
  GY2 = MPU-6050 Board GY-521 [form="♀ (female)" package=THT]
  o4 = 1.3 Zoll OLED I2C 128x64 SSD1306 [package=THT]

nets:
  GND: Part2.GND, GY2.pin2, o4.GND
  5V: Part2.5V, GY2.pin1, o4.VDD
  N1: Part2.A5, GY2.pin3, o4.SCL
  N2: Part2.A4, GY2.pin4, o4.SDA

custom parts:
  MPU-6050 Board GY-521: Acelerometro y Giroscopio MPU-6050 Board GY-521
