# Fritzing sketch receiverfinal (saved by Fritzing 0.8.7b)
breadboards: 1

parts:
  Part6 = Arduino Nano (Rev3.0)
  o5 = 1.3 Zoll OLED I2C 128x64 SSD1306 [package=THT]
  VCC3 = Battery block 9V
  S2 = H-Bridge with L298N
  M3 = DC Motor
  M4 = DC Motor
  Part7 = GY-VL53L0XV2 Laser Ranger Module  # not connected
  A2 = NRF24L01-BO-with-pcb [package=THT]
  U1 = WS2812 RGB LED strip

nets:
  GND: Part6.GND, o5.GND, VCC3.-, S2.GND, A2.GND, U1.GND
  N1: Part6.D2, S2.ENB
  N2: Part6.D3, S2.IN4
  N3: Part6.D4, S2.IN3
  N4: Part6.D5, S2.IN2
  N5: Part6.D6, S2.IN1
  N6: Part6.D7, S2.ENA
  N7: Part6.D8, U1.DIN
  N8: Part6.D9, A2.CE
  N9: Part6.D10, A2.CSN
  N10: Part6.D11/MOSI, A2.M0
  N11: Part6.D12/MISO, A2.M1
  VCC: Part6.VIN, S2.5V, A2.VCC, U1.VCC
  5V: Part6.5V, o5.VDD
  N12: Part6.A7, o5.SDA
  N13: Part6.A5, o5.SCL
  N14: Part6.D13/SCK, A2.SCK
  N15: VCC3.+, S2.12V
  N16: S2.M1-01, M3.pin_2
  N17: S2.M1-02, M3.pin_1
  N18: S2.M2-01, M4.pin_2
  N19: S2.M2-02, M4.pin_1

custom parts:
  H-Bridge with L298N: h-bridge
  GY-VL53L0XV2 Laser Ranger Module: The GY-VL53L0XV2 is based on the VL53L0X from ST Microelectronics, a time-of-flight ranging system integrated into a compact module.
  NRF24L01-BO-with-pcb: NRF24L01-BO breakout board for the NRF24L01. Pcb is present but untested.
  WS2812 RGB LED strip: WS2812 strip
