# Fritzing sketch transmitter_battery (saved by Fritzing 0.8.7b)
breadboards: 1

parts:
  A3 = NRF24L01-BO-with-pcb [package=THT]
  Part3 = Arduino Nano (Rev3.0)
  GY3 = MPU-6050 Board GY-521 [form="♀ (female)" package=THT]
  o5 = 1.3 Zoll OLED I2C 128x64 SSD1306 [package=THT]
  VCC1 = Battery block 9V

nets:
  N1: A3.M0, A3.GND, Part3.D1/TX
  N2: A3.CSN, Part3.D6
  N3: A3.CE, Part3.D10
  GND: Part3.GND, GY3.pin2, o5.GND, VCC1.-
  N4: Part3.VIN, VCC1.+
  5V: Part3.5V, GY3.pin1, o5.VDD
  N5: Part3.A5, GY3.pin3, o5.SCL
  N6: Part3.A4, GY3.pin4, o5.SDA

custom parts:
  NRF24L01-BO-with-pcb: NRF24L01-BO breakout board for the NRF24L01. Pcb is present but untested.
  MPU-6050 Board GY-521: Acelerometro y Giroscopio MPU-6050 Board GY-521
