# Fritzing sketch ws2812 (saved by Fritzing 0.8.7b)
breadboards: 1

parts:
  Part4 = Arduino Nano (Rev3.0)
  U1 = WS2812 RGB LED strip

nets:
  GND: Part4.GND, U1.GND
  5V: Part4.5V, U1.VCC
  N1: Part4.A3, U1.DIN

custom parts:
  WS2812 RGB LED strip: WS2812 strip
