# Fritzing sketch receiver_f (saved by Fritzing 0.8.7b)
breadboards: 1

parts:
  Part3 = Arduino Nano (Rev3.0)
  Part8 = GY-VL53L0XV2 Laser Ranger Module
  U2 = WS2812 RGB LED strip
  S6 = H-Bridge with L298N
  M11 = DC Motor
  M12 = DC Motor
  A4 = NRF24L01-BO-with-pcb [package=THT]
  VCC1 = Battery block 9V

nets:
  N1: Part3.D1/TX, A4.M0, A4.GND
  GND: Part3.GND, Part8.GND, U2.GND, S6.GND, VCC1.-
  N2: Part3.D3, S6.ENB
  N3: Part3.D4, S6.IN4
  N4: Part3.D5, S6.IN3
  N5: Part3.D6, A4.CSN
  N6: Part3.D7, S6.IN2
  N7: Part3.D8, S6.IN1
  N8: Part3.D9, S6.ENA
  N9: Part3.D10, A4.CE
  VIN: Part3.VIN, S6.12V, VCC1.+
  VCC: Part3.5V, Part8.VCC, U2.VCC
  N10: Part3.A5, Part8.SCL
  N11: Part3.A4, Part8.SDA
  N12: Part3.A3, U2.DIN
  N13: S6.M1-01, M11.pin_2
  N14: S6.M1-02, M11.pin_1
  N15: S6.M2-01, M12.pin_2
  N16: S6.M2-02, M12.pin_1

custom parts:
  GY-VL53L0XV2 Laser Ranger Module: The GY-VL53L0XV2 is based on the VL53L0X from ST Microelectronics, a time-of-flight ranging system integrated into a compact module.
  WS2812 RGB LED strip: WS2812 strip
  H-Bridge with L298N: h-bridge
  NRF24L01-BO-with-pcb: NRF24L01-BO breakout board for the NRF24L01. Pcb is present but untested.
